// Logisim project cpu.circ as structural Verilog
module RegisterFile16bit (
  input  [15:0] RegisterData,
  input  [3:0] SelectDestination,
  input  [3:0] SelectRegister1,
  input  [3:0] SelectRegister2,
  input  RegWrite,
  input  Clock,
  output [15:0] Out1,
  output [15:0] Out2
);

  wire and_1_out, select0, select1, select2, select3, select4, select5, select6, select7, select8, select9,
       select10, select11, select12, select13, select14, select15;
  wire [15:0] R0, R1, R2, R3, R4, R5, R6, R7, R8, R9, R10, R11, R12, R13, R14, R15;

  Decoder #(.select(4)) decoder_1 (
    .out0(select0), .out1(select1), .out2(select2), .out3(select3), .out4(select4), .out5(select5),
    .out6(select6), .out7(select7), .out8(select8), .out9(select9), .out10(select10), .out11(select11),
    .out12(select12), .out13(select13), .out14(select14), .out15(select15), .sel(SelectDestination));  // open: en
  and and_1 (and_1_out, RegWrite, Clock);
  Register #(.width(16)) register_1 (.D({16{1'b0}}), .en(1'b1), .Q(R0), .clk(and_1_out));  // open: clr
  Register #(.width(16)) register_2 (.D(RegisterData), .en(select1), .Q(R1), .clk(and_1_out));  // open: clr
  Register #(.width(16)) register_3 (.D(RegisterData), .en(select2), .Q(R2), .clk(and_1_out));  // open: clr
  Register #(.width(16)) register_4 (.D(RegisterData), .en(select3), .Q(R3), .clk(and_1_out));  // open: clr
  Register #(.width(16)) register_5 (.D(RegisterData), .en(select4), .Q(R4), .clk(and_1_out));  // open: clr
  Register #(.width(16)) register_6 (.D(RegisterData), .en(select5), .Q(R5), .clk(and_1_out));  // open: clr
  Register #(.width(16)) register_7 (.D(RegisterData), .en(select6), .Q(R6), .clk(and_1_out));  // open: clr
  Register #(.width(16)) register_8 (.D(RegisterData), .en(select7), .Q(R7), .clk(and_1_out));  // open: clr
  Register #(.width(16)) register_9 (.D(RegisterData), .en(select8), .Q(R8), .clk(and_1_out));  // open: clr
  Register #(.width(16)) register_10 (.D(RegisterData), .en(select9), .Q(R9), .clk(and_1_out));  // open: clr
  Register #(.width(16)) register_11 (.D(RegisterData), .en(select10), .Q(R10), .clk(and_1_out));  // open: clr
  Register #(.width(16)) register_12 (.D(RegisterData), .en(select11), .Q(R11), .clk(and_1_out));  // open: clr
  Register #(.width(16)) register_13 (.D(RegisterData), .en(select12), .Q(R12), .clk(and_1_out));  // open: clr
  Register #(.width(16)) register_14 (.D(RegisterData), .en(select13), .Q(R13), .clk(and_1_out));  // open: clr
  Register #(.width(16)) register_15 (.D(RegisterData), .en(select14), .Q(R14), .clk(and_1_out));  // open: clr
  Register #(.width(16)) register_16 (.D(RegisterData), .en(select15), .Q(R15), .clk(and_1_out));  // open: clr
  Multiplexer #(.select(4), .width(16)) multiplexer_1 (
    .in0(R0), .in1(R1), .in2(R2), .in3(R3), .in4(R4), .in5(R5), .in6(R6), .in7(R7), .in8(R8), .in9(R9),
    .in10(R10), .in11(R11), .in12(R12), .in13(R13), .in14(R14), .in15(R15), .out(Out1), .sel(SelectRegister1));  // open: en
  Multiplexer #(.select(4), .width(16)) multiplexer_2 (
    .in0(R0), .in1(R1), .in2(R2), .in3(R3), .in4(R4), .in5(R5), .in6(R6), .in7(R7), .in8(R8), .in9(R9),
    .in10(R10), .in11(R11), .in12(R12), .in13(R13), .in14(R14), .in15(R15), .out(Out2), .sel(SelectRegister2));  // open: en

  // Notes on the sheet:
  //   The first register is wired to be always zero
endmodule
